# Fritzing sketch BMS (saved by Fritzing 0.9.3b)
breadboards: 1

parts:
  BATTERY_1 = DC Power [voltage=5]
  BATTERY_2 = DC Power [voltage=5]
  U1 = RELAY-2 [package=relay-g5v]
  TO_CIRCUIT = Header 2 [package=jst-2-smd]
  Part1 = Arduino Uno (Rev3)
  R1 = Trimmer Potentiometer [maximum_resistance=10kΩ package=THT]
  R2 = Trimmer Potentiometer [maximum_resistance=10kΩ package=THT]

nets:
  N1: BATTERY_1.V+, U1.1, R1.leg1
  N2: BATTERY_1.V-, BATTERY_2.V-, TO_CIRCUIT.1, Part1.GND, R1.leg2, R2.leg2
  N3: BATTERY_2.V+, U1.10, R2.leg1
  N4: U1.2, Part1.D7
  N5: U1.6, TO_CIRCUIT.2
  N6: Part1.A1, R1.wiper
  N7: Part1.A2, R2.wiper

// code stored in the sketch: Untitled2.ino
/*
Assuming battery B1 to be connected initially and the voltages  as mentioned. 

The pots have been adjusted to give outputs between 0-5v

*/


#define BATTERY1 1   //battery 1 at analog 1 pin
#define BATTERY2 2   //battery 1 at analog 2 pin
#define RELAY    7   //relay at digital pin 7
#define B_HIGH   18  //voltage of battery at full charge
#define B_LOW    16  //voltage of battery at low charge




void setup()
{

pinMode(RELAY, OUTPUT);

}



void loop()
{

int BA1 = analogRead(BATTERY1);
int BA2 = analogRead(BATTERY2);

int cutoff = map(B_LOW, 0, B_HIGH, 0, 1023);

if(BA1 <= cutoff) digitalWrite(RELAY, HIGH);

if(BA2 <= cutoff) digitalWrite(RELAY, LOW);


}
