// Logisim project BLDC.circ as structural Verilog: 3 circuits, main circuit main
module main (
  input  Q1L,
  input  Q1H,
  input  H1,
  input  Q2L,
  input  H2,
  input  Q2H,
  input  H3,
  input  Q3L,
  input  Q3H
);

  wire and_1_out, and_2_out, and_3_out, and_4_out, and_5_out, and_6_out, not_1_out, not_2_out, not_3_out,
       not_4_out, not_5_out, not_6_out;

  not not_1 (not_1_out, H2);
  not not_2 (not_2_out, H1);
  not not_3 (not_3_out, H3);
  not not_4 (not_4_out, H2);
  not not_5 (not_5_out, H1);
  not not_6 (not_6_out, H3);
  and and_1 (and_1_out, not_1_out, H1);
  and and_2 (and_2_out, not_2_out, H2);
  and and_3 (and_3_out, not_3_out, H2);
  and and_4 (and_4_out, not_4_out, H3);
  and and_5 (and_5_out, not_5_out, H3);
  and and_6 (and_6_out, not_6_out, H1);

  // Notes on the sheet:
  //   Q2L
endmodule

module main1 (
  input  H1,
  input  H2,
  input  H3,
  output Q1L,
  output Q1H,
  output Q2L,
  output Q2H,
  output Q3L,
  output Q3H
);
endmodule

module FINAL (
  input  H1,
  input  H2,
  input  H3,
  output Q1L,
  output Q1H,
  output Q2L,
  output Q2H,
  output Q3L,
  output Q3H
);

  wire not_1_out, not_2_out, not_3_out, not_4_out, not_5_out, not_6_out;

  not not_1 (not_1_out, H2);
  not not_2 (not_2_out, H1);
  not not_3 (not_3_out, H3);
  not not_4 (not_4_out, H2);
  not not_5 (not_5_out, H1);
  not not_6 (not_6_out, H3);
  and and_1 (Q1L, H1, not_1_out);
  and and_2 (Q1H, not_2_out, H2);
  and and_3 (Q2L, H2, not_3_out);
  and and_4 (Q2H, not_4_out, H3);
  and and_5 (Q3L, not_5_out, H3);
  and and_6 (Q3H, H1, not_6_out);
endmodule
