# Fritzing sketch KickerCKT (saved by Fritzing 0.9.3b)
breadboards: 1

parts:
  R1 = Resistor [tolerance=±5% resistance=220 package=THT]
  C1 = Electrolytic Capacitor [capacitance=1µF package="100 mil [THT, electrolytic]"]  # not connected
  Q1 = NPN-Transistor [package="TO92 [THT]"]
  R2 = Resistor [tolerance=±5% resistance=220 package=THT]
  L1 = Inductor [package="400 mil [THT]"]
  R3 = Resistor [tolerance=±5% resistance=220 package=THT]
  D1 = Rectifier Diode [part_number=1N4001 package="300 mil [THT]"]
  R4 = Resistor [tolerance=±5% resistance=220 package=THT]
  SIGNAL = AC Power [voltage=5 frequency=60]

nets:
  200V: R1.Pin_0
  N1: R1.Pin_1, L1.pin_0, D1.cathode
  GND: Q1.E, SIGNAL.V-
  N2: Q1.B, R2.Pin_1
  N3: Q1.C, R3.Pin_0, R4.Pin_0
  N4: R2.Pin_0, SIGNAL.V+
  N5: L1.pin_1, R3.Pin_1
  N6: D1.anode, R4.Pin_1
